# Fritzing sketch Lamp002 (saved by Fritzing 0.9.3b)
breadboards: 1

parts:
  Part1 = FTDI Basic Programmer
  U1 = ESP8266 WiFi Module [part_number=ESP8266]
  LED1 = LED - 5mm [color="Red (633nm)" package="5 mm [THT]"]
  R1 = Resistor [tolerance=±5% resistance=220 package=THT]

nets:
  N1: Part1.RXI, U1.TXD
  N2: Part1.TXO, U1.RXD
  N3: Part1.POWER, U1.VCC, U1.CH_PD
  GND: Part1.GND, U1.GND, R1.Pin_1
  N4: U1.GPIO_2, LED1.anode
  N5: LED1.cathode, R1.Pin_0

custom parts:
  ESP8266 WiFi Module: Generic WiFi Module based on the ESP8266 with onboard PCB antenna and UART communications
